# Fritzing sketch montagem (saved by Fritzing 0.9.3b)

parts:
  U1 = ESP8266 NodeMCU LoLin module
  LED1 = LED - 5mm [color="Red (633nm)" package="5 mm [THT]"]
  Componente1 = SRF05 Ultrasonic Rangefinder

nets:
  N1: U1.D5, Componente1.Echo
  N2: U1.D6, Componente1.Trig
  N3: U1.D8, LED1.anode
  GND: U1.GND, LED1.cathode, Componente1.GND
  VIN: U1.Vin, Componente1.VCC

custom parts:
  ESP8266 NodeMCU LoLin module: ESP8266 based NodeMCU
